# Fritzing sketch schema (saved by Fritzing 0.9.3b)
perfboards: 1

parts:
  Raspberry_Pi_1 = Raspberry Pi 3 [part_number=RPI-3-V1.2]
  BTN_1 = Round Pushbutton  # not connected
  R1 = Resistor [tolerance=±5% resistance=10k package="2010 [SMD]"]  # not connected
  R2 = Resistor [tolerance=±5% resistance=1k package="2010 [SMD]"]  # not connected
  Grove1 = Grove 4 Digit Display
  S3 = Round Pushbutton  # not connected
  R3 = Resistor [tolerance=±5% resistance=1k package="2010 [SMD]"]  # not connected
  R4 = Resistor [tolerance=±5% resistance=10k package="2010 [SMD]"]  # not connected
  RC522 = RFID-RC522-v2

nets:
  3V3: Raspberry_Pi_1.3v3, Raspberry_Pi_1.3V3
  GND: Raspberry_Pi_1.GND, Grove1.GND, RC522.GND
  N1: Raspberry_Pi_1.GIPO10, RC522.MISO
  N2: Raspberry_Pi_1.GIPO9, RC522.IRQ
  N3: Raspberry_Pi_1.GIPO11, RC522.MOSI
  N4: Raspberry_Pi_1.GIPO21, Grove1.CLK
  N5: Raspberry_Pi_1.GIPO20, Grove1.DIO
  N6: Raspberry_Pi_1.GIPO8, RC522.SCK
  N7: Raspberry_Pi_1.GIPO25, RC522.RST
  5V: Raspberry_Pi_1.5V, Grove1.VCC, RC522.3.3V

custom parts:
  RFID-RC522-v2: A simple China made RFID-RC522 Reader; do check the pin labels, as this is a MFRC522 based clone.
